# Fritzing sketch fancyLED (saved by Fritzing 0.9.3b)
breadboards: 1

parts:
  Part1 = Adafruit Metro M0 Express
  LED1 = smd LED [color="White (6500K)" package="1206 [SMD]"]
  LED2 = smd LED [color="Yellow (585nm)" package="1206 [SMD]"]
  LED3 = smd LED [color="Orange (620nm)" package="1206 [SMD]"]
  LED4 = smd LED [color="Blue (470nm)" package="1206 [SMD]"]
  LED5 = smd LED [color="Green (555nm)" package="1206 [SMD]"]
  LED6 = smd LED [color="Red (633nm)" package="1206 [SMD]"]
  R1 = Resistor [tolerance=±1% resistance=220 package="2512 [SMD]"]
  R2 = Resistor [tolerance=±1% resistance=220 package="2512 [SMD]"]
  R3 = Resistor [tolerance=±1% resistance=220 package="2512 [SMD]"]
  R4 = Resistor [tolerance=±1% resistance=220 package="2512 [SMD]"]
  R5 = Resistor [tolerance=±1% resistance=220 package="2512 [SMD]"]
  R6 = Resistor [tolerance=±1% resistance=220 package="2512 [SMD]"]

nets:
  N1: Part1.GND, R1.Pin_0, R2.Pin_0, R3.Pin_0, R4.Pin_0, R5.Pin_0, R6.Pin_0
  N2: Part1.D13, LED6.anode
  N3: Part1.D12, LED5.anode
  N4: Part1.D11, LED4.anode
  N5: Part1.D10, LED3.anode
  N6: Part1.D9, LED2.anode
  N7: Part1.D8, LED1.anode
  N8: LED1.cathode, R1.Pin_1
  N9: LED2.cathode, R2.Pin_1
  N10: LED3.cathode, R3.Pin_1
  N11: LED4.cathode, R4.Pin_1
  N12: LED5.cathode, R5.Pin_1
  N13: LED6.cathode, R6.Pin_1

custom parts:
  Adafruit Metro M0 Express: Metro is our series of microcontroller boards for use with the Arduino IDE. This new Metro board looks a whole lot like our original Metro 328, but with a huge upgrade. Instead of the ATmega328, this Metro features a ATSAMD21G18 chip, an ARM Cortex M0+. It's our first Metro that is designed for use with CircuitPython! CircuitPython is our beginner-oriented flavor of MicroPython - and as the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
