# Fritzing sketch lcd (saved by Fritzing 0.9.3b)
breadboards: 1

parts:
  Part1 = Adafruit Metro M0 Express
  S1 = Pushbutton [package="[THT]"]
  S2 = Pushbutton [package="[THT]"]
  S3 = Pushbutton [package="[THT]"]
  LCD1 = LCD screen
  R1 = Resistor [tolerance=±5% resistance=10k package="0603 [SMD]"]
  R2 = Resistor [tolerance=±5% resistance=10k package="0603 [SMD]"]
  R3 = Resistor [tolerance=±5% resistance=10 package="0603 [SMD]"]

nets:
  N1: Part1.SCL, LCD1.VSS
  N2: Part1.SDA, LCD1.VDD
  N3: Part1.D13, Part1.D12, Part1.D10, Part1.+5V, S1.Pin_1, S1.Pin_2, S2.Pin_1, S2.Pin_2, S3.Pin_1, S3.Pin_2, LCD1.V0
  N4: Part1.GND, LCD1.RS, R1.Pin_1, R2.Pin_1, R3.Pin_1
  N5: S1.Pin_3, S1.Pin_4, R1.Pin_0
  N6: S2.Pin_3, S2.Pin_4, R2.Pin_0
  N7: S3.Pin_3, S3.Pin_4, R3.Pin_0

custom parts:
  Adafruit Metro M0 Express: Metro is our series of microcontroller boards for use with the Arduino IDE. This new Metro board looks a whole lot like our original Metro 328, but with a huge upgrade. Instead of the ATmega328, this Metro features a ATSAMD21G18 chip, an ARM Cortex M0+. It's our first Metro that is designed for use with CircuitPython! CircuitPython is our beginner-oriented flavor of MicroPython - and as the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
