# Fritzing sketch photo_interrupter (saved by Fritzing 0.9.3b)
breadboards: 1

parts:
  Q1 = PHOTOTRANSISTOR REFLECTIVE OBJECT SENSOR [package=qrb1114-side]
  Part1 = Adafruit Metro M0 Express

nets:
  N1: Q1.A, Part1.GND
  N2: Q1.C, Q1.E, Part1.+5V
  N3: Q1.K, Part1.D12

custom parts:
  Adafruit Metro M0 Express: Metro is our series of microcontroller boards for use with the Arduino IDE. This new Metro board looks a whole lot like our original Metro 328, but with a huge upgrade. Instead of the ATmega328, this Metro features a ATSAMD21G18 chip, an ARM Cortex M0+. It's our first Metro that is designed for use with CircuitPython! CircuitPython is our beginner-oriented flavor of MicroPython - and as the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
