# Fritzing sketch sensor (saved by Fritzing 0.9.3b)
breadboards: 1

parts:
  HC-SR04_Sensor_1 = HC-SR04 Ultrasonic Distance Sensor
  Part1 = Adafruit Metro M0 Express

nets:
  VCC: HC-SR04_Sensor_1.VCC, Part1.+5V
  N1: HC-SR04_Sensor_1.TRIG, Part1.D9
  N2: HC-SR04_Sensor_1.ECHO, Part1.D10
  GND: HC-SR04_Sensor_1.GND, Part1.GND

custom parts:
  Adafruit Metro M0 Express: Metro is our series of microcontroller boards for use with the Arduino IDE. This new Metro board looks a whole lot like our original Metro 328, but with a huge upgrade. Instead of the ATmega328, this Metro features a ATSAMD21G18 chip, an ARM Cortex M0+. It's our first Metro that is designed for use with CircuitPython! CircuitPython is our beginner-oriented flavor of MicroPython - and as the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
